# Fritzing sketch door_closer (saved by Fritzing 0.9.3b)
circuit board: 8.46667cm x 5.64444cm
breadboards: 1

parts:
  U1 = NodeMCU V1.0
  OMRON1 = OMRON PCB Power Relay – G5LE [part_number="G5LE-1\n" package=THT]
  Q1 = npn-Powertransistor [package="TO220 [THT]"]
  R1 = Resistor [tolerance=±5% resistance=220 package="1206 [SMD]"]
  SG1 = Buzzer 12mm [package=buzzer-12mm-ns-kit]

nets:
  N1: U1.D4, SG1.1
  N2: U1.3V3, OMRON1.COIL1
  N3: U1.GND, Q1.emitter, SG1.2
  N4: U1.D7, R1.Pin_0
  N5: OMRON1.COIL2, Q1.collector
  N6: Q1.base, R1.Pin_1

custom parts:
  NodeMCU V1.0: ESP8266 based NodeMCU
